# Fritzing sketch DectorRuidos (saved by Fritzing 0.9.3b)
breadboards: 1

parts:
  Componente1 = Arduino Uno (Rev3)
  R2 = Resistor [tolerance=±5% resistance=220 package="0402 [SMD]"]
  R3 = Resistor [tolerance=±5% resistance=220 package="0402 [SMD]"]
  R4 = Resistor [tolerance=±5% resistance=220 package="0402 [SMD]"]
  R5 = Resistor [tolerance=±5% resistance=220 package="0402 [SMD]"]
  R6 = Resistor [tolerance=±5% resistance=220 package="0402 [SMD]"]
  R7 = Resistor [tolerance=±5% resistance=220 package="0402 [SMD]"]
  R8 = Resistor [tolerance=±5% resistance=220 package="0402 [SMD]"]
  R9 = Resistor [tolerance=±5% resistance=220 package="0402 [SMD]"]
  R11 = Resistor [tolerance=±5% resistance=220 package="0402 [SMD]"]
  R12 = Resistor [tolerance=±5% resistance=220 package="0402 [SMD]"]
  Part1 = KY-037 High Sensitivity Sound Detection Module [package="Breakout board"]
  D1 = LED_BARGRAPH_10 [package=led_bargaph_10]

nets:
  N1: Componente1.A0, Part1.A0
  N2: Componente1.D8, R6.Pin_0, R6.Pin_1, D1.E_A
  N3: Componente1.D9_PWM, R5.Pin_0, R5.Pin_1, D1.D_A
  N4: Componente1.D10_PWM/SS, R4.Pin_0, R4.Pin_1, D1.C_A
  N5: Componente1.D11_PWM/MOSI, R3.Pin_0, R3.Pin_1, D1.B_A
  N6: Componente1.D12/MISO, R2.Pin_0, R2.Pin_1, D1.A_A
  N7: Componente1.D2, Part1.D0
  N8: Componente1.D3_PWM, R7.Pin_0, R7.Pin_1, D1.J_A
  N9: Componente1.D4, R8.Pin_0, R8.Pin_1, D1.I_A
  N10: Componente1.D5_PWM, R9.Pin_0, R9.Pin_1, D1.H_A
  N11: Componente1.D6_PWM, R11.Pin_0, R11.Pin_1, D1.G_A
  N12: Componente1.D7, R12.Pin_0, R12.Pin_1, D1.F_A
  N13: Componente1.5V, Part1.+
  N14: Componente1.GND, Part1.G, D1.J_C, D1.I_C, D1.H_C, D1.G_C, D1.F_C, D1.E_C, D1.D_C, D1.C_C, D1.B_C, D1.A_C

custom parts:
  KY-037 High Sensitivity Sound Detection Module: KY-037 high sensitivity sound detection module is an analog/digital sensor that uses a condenser microphone to observe changes in environment noise.
